# Fritzing sketch 555-Die-2 (saved by Fritzing 0.9.2b)
breadboards: 1

parts:
  LED1 = LED - 5mm [color="Red (633nm)" package="5 mm [THT]"]
  LED4 = LED - 5mm [color="Red (633nm)" package="5 mm [THT]"]
  LED2 = LED - 5mm [color="Red (633nm)" package="5 mm [THT]"]
  LED7 = LED - 5mm [color="Red (633nm)" package="5 mm [THT]"]
  Q1 = PNP-Transistor [package="TO92 [THT]"]
  Q2 = NPN-Transistor [package="TO92 [THT]"]
  Q3 = NPN-Transistor [package="TO92 [THT]"]
  Q4 = NPN-Transistor [package="TO92 [THT]"]
  U1 = 555 Timer [package="DIP8 [THT]"]
  C1 = Ceramic Capacitor [capacitance=100nF package="100 mil [THT, multilayer]"]
  R1 = Resistor [tolerance=±5% resistance=1k package=THT]
  C2 = Electrolytic Capacitor [capacitance=10µF package="100 mil [THT, electrolytic]"]
  R2 = Resistor [tolerance=±5% resistance=2.2k package=THT]
  U2 = IC, DIP package, 16 pins [chip_label="IC 4017"]
  R3 = Resistor [tolerance=±5% resistance=33k package=THT]
  R4 = Resistor [tolerance=±5% resistance=33k package=THT]
  D1 = Diode [package=diode-1n4148]
  R5 = Resistor [tolerance=±5% resistance=33k package=THT]
  R6 = Resistor [tolerance=±5% resistance=33k package=THT]
  D2 = Diode [package=diode-1n4148]
  R7 = Resistor [tolerance=±5% resistance=33k package=THT]
  R8 = Resistor [tolerance=±5% resistance=33k package=THT]
  R9 = Resistor [tolerance=±5% resistance=33k package=THT]
  R10 = Resistor [tolerance=±5% resistance=150 package=THT]
  LED6 = LED - 5mm [color="Red (633nm)" package="5 mm [THT]"]
  LED5 = LED - 5mm [color="Red (633nm)" package="5 mm [THT]"]
  R11 = Resistor [tolerance=±5% resistance=150 package=THT]
  LED3 = LED - 5mm [color="Red (633nm)" package="5 mm [THT]"]
  R12 = Resistor [tolerance=±5% resistance=150 package=THT]
  R13 = Resistor [tolerance=±5% resistance=330 package=THT]

nets (from the schematic view):
  N1: LED1.cathode, LED6.anode
  N2: LED1.anode, Q1.C
  N3: LED4.cathode, Q3.C
  N4: LED4.anode, LED3.cathode
  N5: LED2.cathode, Q2.C
  N6: LED2.anode, LED5.cathode
  N7: LED7.cathode, Q4.C
  N8: LED7.anode, R13.Pin_0
  9V: Q1.E, U1.Reset, U1.Vcc_Supply_Voltage, R1.Pin_1, U2.pin16, R11.Pin_1, R12.Pin_1, R13.Pin_1
  N9: Q1.B, R3.Pin_1
  GND: Q2.E, Q3.E, Q4.E, U1.Ground, C1.0, C2.-, U2.pin8, U2.pin13, R10.Pin_0
  N10: Q2.B, Q3.B, R6.Pin_1, R7.Pin_1, R9.Pin_1
  N11: Q4.B, D1.C
  N12: U1.Trigger, U1.Threshold, C2.+, R2.Pin_1
  N13: U1.Output, U2.pin14
  N14: U1.Control_Voltage, C1.1
  N15: U1.Discharge, R1.Pin_0, R2.Pin_0
  N16: U2.pin1, R9.Pin_0
  N17: U2.pin3, R3.Pin_0, R4.Pin_1
  N18: U2.pin4, R5.Pin_0
  N19: U2.pin5, U2.pin15
  N20: U2.pin7, R6.Pin_0
  N21: U2.pin10, D2.A
  N22: R4.Pin_0, D1.A, R5.Pin_1, R8.Pin_1
  N23: D2.C, R7.Pin_0, R8.Pin_0
  N24: R10.Pin_1, LED6.cathode
  N25: LED5.anode, R11.Pin_0
  N26: LED3.anode, R12.Pin_0
