# Fritzing sketch 555-Die (saved by Fritzing 0.9.2b)
circuit board: 7.52311cm x 4.90357cm
breadboards: 1

parts:
  LED1 = LED - 5mm [color="Red (633nm)" package="5 mm [THT]"]
  LED6 = LED - 5mm [color="Red (633nm)" package="5 mm [THT]"]
  LED3 = LED - 5mm [color="Red (633nm)" package="5 mm [THT]"]
  LED4 = LED - 5mm [color="Red (633nm)" package="5 mm [THT]"]
  LED2 = LED - 5mm [color="Red (633nm)" package="5 mm [THT]"]
  LED5 = LED - 5mm [color="Red (633nm)" package="5 mm [THT]"]
  LED7 = LED - 5mm [color="Red (633nm)" package="5 mm [THT]"]
  Q1 = PNP-Transistor [package="TO92 [THT]"]
  Q2 = NPN-Transistor [package="TO92 [THT]"]
  Q3 = NPN-Transistor [package="TO92 [THT]"]
  Q4 = NPN-Transistor [package="TO92 [THT]"]
  U1 = 555 Timer [package="DIP8 [THT]"]
  C1 = Ceramic Capacitor [capacitance=100nF package="100 mil [THT, multilayer]"]
  R1 = Resistor [tolerance=±5% resistance=1k package=THT]
  C2 = Electrolytic Capacitor [capacitance=10µF package="100 mil [THT, electrolytic]"]
  R2 = Resistor [tolerance=±5% resistance=2.2k package=THT]
  U2 = IC, DIP package, 16 pins [chip_label="IC 4017"]

nets:
  N1: LED1.cathode, LED6.anode
  N2: LED1.anode, Q1.C
  GND: LED6.cathode, Q2.E, Q3.E, Q4.E, U1.Ground, C1.0, C2.-, U2.pin8, U2.pin13
  N3: LED3.cathode, LED4.anode
  9V: LED3.anode, LED5.anode, LED7.anode, Q1.E, U1.Reset, U1.Vcc_Supply_Voltage, R1.Pin_1, U2.pin16
  N4: LED4.cathode, Q3.C
  N5: LED2.cathode, Q2.C
  N6: LED2.anode, LED5.cathode
  N7: LED7.cathode, Q4.C
  N8: U1.Trigger, U1.Threshold, C2.+, R2.Pin_1
  N9: U1.Output, U2.pin14
  N10: U1.Control_Voltage, C1.1
  N11: U1.Discharge, R1.Pin_0, R2.Pin_0
  N12: U2.pin5, U2.pin15
