# Fritzing sketch Arduino_128_64 (saved by Fritzing 0.9.2b)
circuit board: 5.41099cm x 6.30096cm
breadboards: 1

parts:
  R1 = Resistor [tolerance=±5% resistance=220 package=THT]
  R2 = Rotary Potentiometer (Small) [maximum_resistance=100kΩ package=THT]
  Part1 = Arduino Nano (Rev3.0) (ICSP)
  J2 = Power Jack [package=power_jack_pth_lock]
  J3 = female pin header, 20 pins [form="♀ (female)"]

nets:
  N1: R1.Pin_0, Part1.5V, J2.PWR, J3.pin19
  N2: R1.Pin_1, J3.pin2
  N3: R2.leg1, J3.pin3
  N4: R2.wiper, J3.pin18
  GND: R2.leg2, Part1.GND, J2.GND, J3.pin1, J3.pin20
  N5: Part1.D10, J3.pin17
  N6: Part1.D11/MOSI, J3.pin16
  N7: Part1.D13/SCK, J3.pin15
