# Fritzing sketch LED-Tester (saved by Fritzing 0.9.2b)
circuit board: 2.48357cm x 1.74004cm
breadboards: 1

parts:
  S1 = Toggle Switch [package=THT]
  R1 = Resistor [tolerance=±5% resistance=100k package=THT]
  LED1 = LED - 5mm [color="Red (633nm)" package="5 mm [THT]"]
  LED2 = LED - 5mm [color="Red (633nm)" package="5 mm [THT]"]
  R2 = Resistor [tolerance=±5% resistance=470 package=THT]
  V1 = DC Power [voltage=9V]

nets:
  N1: S1.L1, R1.Pin_0, LED1.anode
  N2: S1.COM, R2.Pin_1
  N3: S1.L2, R1.Pin_1, LED2.anode
  N4: LED1.cathode, LED2.cathode, V1.V-
  N5: R2.Pin_0, V1.V+
