# Fritzing sketch Proximity-Badge-DRC0 (saved by Fritzing 0.9.2b)
circuit board: 6.74094cm x 6.22445cm
breadboards: 1

parts:
  LCD1 = LCD screen
  R1 = Resistor [tolerance=±5% resistance=220 package=THT]
  Arduino_Nano = Arduino Nano (Rev3.0)
  R2 = Rotary Potentiometer (Small) [maximum_resistance=10kΩ package=THT]
  Ultrasonic = female pin header, 4 pins [form="♀ (female)"]
  6-9V_Gnd = female pin header, 2 pins [form="♀ (female)"]
  Gnd_Vcc_Din = female pin header, 3 pins [form="♀ (female)"]

nets:
  VSS: LCD1.VSS, LCD1.R/W, LCD1.LED-, Arduino_Nano.GND, R2.leg2, Ultrasonic.pin1, 6-9V_Gnd.pin2, Gnd_Vcc_Din.pin3
  VDD: LCD1.VDD, R1.Pin_1, Arduino_Nano.5V, R2.leg1, Ultrasonic.pin4, Gnd_Vcc_Din.pin2
  N1: LCD1.V0, R2.wiper
  N2: LCD1.RS, Arduino_Nano.D11/MOSI
  N3: LCD1.E, Arduino_Nano.D10
  N4: LCD1.DB4, Arduino_Nano.D9
  N5: LCD1.DB5, Arduino_Nano.D8
  N6: LCD1.DB6, Arduino_Nano.D7
  N7: LCD1.DB7, Arduino_Nano.D6
  N8: LCD1.LED+, R1.Pin_0
  N9: Arduino_Nano.D2, Gnd_Vcc_Din.pin1
  N10: Arduino_Nano.D12/MISO, Ultrasonic.pin3
  N11: Arduino_Nano.VIN, 6-9V_Gnd.pin1
  N12: Arduino_Nano.D13/SCK, Ultrasonic.pin2
