# Fritzing sketch Transistor-Tester (saved by Fritzing 0.9.2b)
circuit board: 2.79642cm x 3.24731cm
breadboards: 1

parts:
  LED1 = LED - 5mm [color="Red (633nm)" package="5 mm [THT]"]
  C1 = Electrolytic Capacitor [capacitance=1µF package="100 mil [THT, electrolytic]"]
  R1 = Resistor [tolerance=±5% resistance=22 package=THT]
  R2 = Resistor [tolerance=±5% resistance=1k package=THT]
  R3 = Resistor [tolerance=±5% resistance=330 package=THT]
  Q2 = NPN-Transistor [package="TO92 [THT]"]
  Q1 = NPN-Transistor [package="TO92 [THT]"]

nets:
  N1: LED1.cathode, Q1.C
  5V: LED1.anode, R3.Pin_1
  N2: C1.-, R1.Pin_1, Q1.E
  N3: C1.+, R3.Pin_0, Q2.B
  GND: R1.Pin_0, Q2.E
  N4: R2.Pin_0, Q2.C
  N5: R2.Pin_1, Q1.B
